# Fritzing sketch ArdunioTimeHackerClock (saved by Fritzing 0.9.3b)

parts:
  Part8 = Adafruit Feather 32u4 Bluefruit [part_number="Adafruit #2829"]
  Part9 = Lithium Ion Polymer Battery 3.7v 100mAh [part_number=1570]  # not connected
  ZS-042_RTC1 = ZS-042 RTC Module
  Part10 = ws2812b [package="smd 2812b"]

nets:
  GND: Part8.GND, ZS-042_RTC1.GND
  +3V3: Part8.+3V3, ZS-042_RTC1.VCC
  N1: Part8.6, Part10.DIN
  N2: Part8.3, ZS-042_RTC1.SCL
  N3: Part8.2, ZS-042_RTC1.SDA

custom parts:
  Adafruit Feather 32u4 Bluefruit: This is the Adafruit Feather 32u4 Bluefruit - our take on an 'all-in-one' Arduino-compatible + Bluetooth Low Energy with built in USB and battery charging. Its an Adafruit Feather 32u4 with a BTLE module, ready to rock! We have other boards in the Feather family, check'em out here. Bluetooth Low Energy is the hottest new low-power, 2.4GHz spectrum wireless protocol. In particular, its the only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
  Lithium Ion Polymer Battery 3.7v 100mAh: Lithium ion polymer (also known as 'lipo' or 'lipoly') batteries are thin, light and powerful. The output ranges from 4.2V when completely charged to 3.7V. This battery has a capacity of ~100mAh for a total of about 0.4 Wh. The batteries come pre-attached with a genuine 2-pin JST-PH connector as shown and include the necessary protection circuitry.
